# Fritzing sketch pcb (saved by Fritzing 0.9.3b)
circuit board: 8.46667cm x 5.64444cm
breadboards: 1

parts:
  Part1 = Adafruit MPR121
  Level_Shifter = 74AHCT125 [part_number=SN74AHCT125 package=dil14]
  Teensy_3_1 = Teensy 3.2
  +/- = Battery
  J1 = female pin header, 4 pins [form="♀ (female)"]
  +/-1 = Battery

nets:
  GND: Part1.GND, Level_Shifter.1OE, Level_Shifter.2OE, Level_Shifter.GND, Level_Shifter.3A, Level_Shifter.4A, Teensy_3_1.GND, +/-.-, J1.pin4, +/-1.-
  VIN: Part1.VIN, Level_Shifter.VCC, Teensy_3_1.Vin, +/-.+, J1.pin1, +/-1.+
  N1: Part1.SDA, Teensy_3_1.A4/D18
  N2: Part1.SCL, Teensy_3_1.A5/D19
  N3: Part1.IRQ, Teensy_3_1.A2/D16
  N4: Level_Shifter.1A, Teensy_3_1.D7
  N5: Level_Shifter.1Y, J1.pin2
  N6: Level_Shifter.2A, Teensy_3_1.A0/D14
  N7: Level_Shifter.2Y, J1.pin3

custom parts:
  Adafruit MPR121: Add lots of touch sensors to your next microcontroller project with this easy-to-use 12-channel capacitive touch sensor breakout board, starring the MPR121. This chip can handle up to 12 individual touch pads. The MPR121 has support for only I2C, which can be implemented with nearly any microcontroller. You can select one of 4 addresses with the ADDR pin, for a total of 48 capacitive touch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
  74AHCT125: Quad Level-Shifter (3V to 5V) Quadruple Bus Buffer Gates With 3-State Outputs
  Teensy 3.2: The Teensy is a complete USB-based microcontoller development system, in a very small footprint, capable of implementing many types of projects. All programming is done via the USB port. No special programmer is needed, only a standard micro-USB cable and a PC or Macintosh with a USB port. It has a USB keyboard/mouse/joystick emulation stack and can be programmed through Arduino IDE. I removed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
